// Digital circuit alu_4.dig as structural Verilog
module alu_4 (
  input  [3:0] x,
  input  [3:0] y,
  input  op,
  output [3:0] s
);

  wire [3:0] add_4_1_s, sub_4_1_s;

  add_4 add_4_1 (.x(x), .y(y), .s(add_4_1_s));
  sub_4 sub_4_1 (.x(x), .y(y), .s(sub_4_1_s));
  Multiplexer #(.Bits(4)) multiplexer_1 (.sel(op), .in_0(add_4_1_s), .in_1(sub_4_1_s), .out(s));

  // Notes on the sheet:
  //   op: op=0 => add
  //   op=1 => sub
endmodule
