// Digital circuit counter_4.dig as structural Verilog
module counter_4 (
  input  clk,
  input  inc,
  input  rst,
  output [3:0] s
);

  wire [3:0] inc_4_1_s, multiplexer_1_out, multiplexer_2_out;

  inc_4 inc_4_1 (.x(s), .s(inc_4_1_s));
  Multiplexer #(.Bits(4)) multiplexer_1 (.sel(inc), .in_0(s), .in_1(inc_4_1_s), .out(multiplexer_1_out));
  Multiplexer #(.Bits(4)) multiplexer_2 (.sel(rst), .in_0(multiplexer_1_out), .in_1(4'b0000), .out(multiplexer_2_out));
  reg_4 reg_4_1 (.in(multiplexer_2_out), .clk(clk), .load(1'b1), .out(s));

  // Notes on the sheet:
  //   s: output
endmodule
