// Digital circuit cpu_4.dig as structural Verilog
module cpu_4 (
);

  reg_4 RegA ();  // open: in, clk, load, out
  counter_4 PC ();  // open: clk, inc, rst, s
  alu_4 alu_4_1 ();  // open: x, y, op, s, zr
endmodule
