// Digital circuit hack_fpga.dig as structural Verilog
module hack_fpga (
  input  btn1,
  input  clk,
  output a,
  output b,
  output c,
  output d,
  output e,
  output f,
  output g,
  output d4,
  output d3,
  output d2,
  output d1
);

  wire u_clkdiv_cpu_clk_out, u_clkdiv_disp_clk_out;

  clkdiv_disp #(.applicationType("IVERILOG"), .CodeFile("clkdiv_disp.v")) u_clkdiv_disp (
    .clk(clk), .clk_out(u_clkdiv_disp_clk_out));
  clkdiv_cpu #(.applicationType("IVERILOG"), .CodeFile("clkdiv_cpu.v")) u_clkdiv_cpu (
    .clk(clk), .clk_out(u_clkdiv_cpu_clk_out));
  hack hack_1 (
    .btn1(btn1), .clk_cpu(u_clkdiv_cpu_clk_out), .clk_disp(u_clkdiv_disp_clk_out), .a(a), .b(b), .c(c),
    .d(d), .e(e), .f(f), .g(g), .d4(d4), .d3(d3), .d2(d2), .d1(d1));
endmodule
