// Digital circuit computer.dig as structural Verilog
module computer (
);

  mem Memory ();  // open: in, addr, load, clk, out
  ROM #(.AddrBits(15), .Bits(16)) ROM32K (.sel(1'b1));  // open: A, D
endmodule
