// Digital circuit cpu.dig as structural Verilog
module cpu (
  input  [15:0] instr,
  input  clk,
  input  [15:0] inM,
  input  rst,
  output [15:0] outM,
  output writeM,
  output [14:0] addrM,
  output [15:0] PC
);

  wire ac, jmp_1_jmp, ng, not_2_out, or_1_out, zr;
  wire [15:0] multiplexer_1_out, multiplexer_2_out, RegD_p4;
  wire [15:15] RegA_p4;

  not not_1 (ac, instr[15]);
  Multiplexer #(.Bits(16)) multiplexer_1 (.sel(ac), .in_0(outM), .in_1(instr), .out(multiplexer_1_out));
  or or_1 (or_1_out, ac, instr[5]);
  // reg_16 RegA: pin names not known; wires that end beside it: multiplexer_1_out, clk, or_1_out, {RegA_p4[15], addrM}
  not not_2 (not_2_out, jmp_1_jmp);
  counter_16 u_PC (.x({RegA_p4[15], addrM}), .load(jmp_1_jmp), .clk(clk), .inc(not_2_out), .rst(rst), .s(PC));
  Multiplexer #(.Bits(16)) multiplexer_2 (
    .sel(instr[12]), .in_0({RegA_p4[15], addrM}), .in_1(inM), .out(multiplexer_2_out));
  // reg_16 RegD: pin names not known; wires that end beside it: outM, clk, instr[4], RegD_p4
  jmp jmp_1 (.j0(instr[0]), .j1(instr[1]), .j2(instr[2]), .ng(ng), .zr(zr), .JMP(jmp_1_jmp));
  alu_16 ALU (.op(instr[11:6]), .x(RegD_p4), .y(multiplexer_2_out), .s(outM), .zr(zr), .ng(ng));
  and and_1 (writeM, ac, instr[3]);

  // Other names for the same wires on the sheet: j[2:0] = instr[2:0]; d[2:0] = instr[5:3]; d0 = instr[3];
  //   d1 = instr[4]; d2 = instr[5]; c[5:0] = instr[11:6]; a = instr[12]

  // Notes on the sheet:
  //   outM: written to RAM[addressM], instruction's M output
  //   inM: instruction's M input, contents of RAM[A]
  //   writeM: write to the memory?
  //   addrM: at which address to write?
  //   PC: address of next instr
  //   instruction decoding
  //   In case of an A-instruction, the instruction bits are interpreted as a binary value that should be loaded
  //   into the A register. In case of a C-instruction, the instruction is treated as a
  //   capsule of control bits 1xxaccccccdddjjj, as follows. The a and cccccc bits code
  //   the comp part of the instruction; the ddd bits code the dest part of the
  //   instruction; the jjj bits code the jump part of the instruction. The xx bits are ignored.
  //   if a = 0, ALU'S y comes from A
  //   if a =1 it comes from memory via inM
  //   ac = 0 => a-instr
  //   ac = 1 => c-instr
  //   d2 d1 d0 | dest
  //   ---------|------
  //   0  0  0  | null
  //   0  0  1  | RAM[A] (M)
  //   0  1  0  | D
  //   0  1  1  | DM
  //   1  0  0  | A
  //   1  0  1  | AM
  //   1  1  0  | AD
  //   1  1  1  | ADM
  //   a-instr or c-instr
  //   in effect, whether to store:
  //   d0 => M, d1 => D, d2 => A
  //   ALSO when a-instr
  //   RegA should store
  //   if jump: PC=A else: PC++, thus:
  //   J | inc | load
  //   --------------
  //   0 | 0 | 1
  //   1 | 1 | 0
  //   jump
  //   ignore the ac (MSB)
endmodule
