// Digital circuit reg_16.dig as structural Verilog
module reg_16 (
  input  [15:0] d,
  input  clk,
  input  l,
  output [15:0] q
);

  \bit  bit_1 (.d(d[0]), .rw(l), .clk(clk), .q(q[0]));
  \bit  bit_2 (.d(d[1]), .rw(l), .clk(clk), .q(q[1]));
  \bit  bit_3 (.d(d[2]), .rw(l), .clk(clk), .q(q[2]));
  \bit  bit_4 (.d(d[3]), .rw(l), .clk(clk), .q(q[3]));
  \bit  bit_5 (.d(d[4]), .rw(l), .clk(clk), .q(q[4]));
  \bit  bit_6 (.d(d[5]), .rw(l), .clk(clk), .q(q[5]));
  \bit  bit_7 (.d(d[6]), .rw(l), .clk(clk), .q(q[6]));
  \bit  bit_8 (.d(d[7]), .rw(l), .clk(clk), .q(q[7]));
  \bit  bit_9 (.d(d[8]), .rw(l), .clk(clk), .q(q[8]));
  \bit  bit_10 (.d(d[9]), .rw(l), .clk(clk), .q(q[9]));
  \bit  bit_11 (.d(d[10]), .rw(l), .clk(clk), .q(q[10]));
  \bit  bit_12 (.d(d[11]), .rw(l), .clk(clk), .q(q[11]));
  \bit  bit_13 (.d(d[12]), .rw(l), .clk(clk), .q(q[12]));
  \bit  bit_14 (.d(d[13]), .rw(l), .clk(clk), .q(q[13]));
  \bit  bit_15 (.d(d[14]), .rw(l), .clk(clk), .q(q[14]));
  \bit  bit_16 (.d(d[15]), .rw(l), .clk(clk), .q(q[15]));

  // Notes on the sheet:
  //   d: data
  //   l: load
  //   q: output
endmodule
